// Digital circuit address.dig as structural Verilog
module address (
  input  A7,
  input  A8,
  input  A9,
  input  A10,
  input  A11,
  input  A12,
  input  A13,
  input  A14,
  input  A15,
  input  A16,
  input  A17,
  input  A18,
  input  A19,
  input  A20,
  input  A21,
  input  A22,
  input  A23,
  output nRAM_EXT,
  output nROM,
  output nIO,
  output nRAM
);

  wire nand_1_out, nand_2_out, nand_3_out, nand_4_out, nand_5_out, nand_6_out, not_1_out, not_2_out,
       not_3_out, not_4_out, not_5_out, not_6_out, not_7_out, not_8_out, or_1_out;

  not not_1 (not_1_out, A23);
  not not_2 (not_2_out, A22);
  not not_3 (not_3_out, A21);
  not not_4 (not_4_out, A20);
  not not_5 (not_5_out, A19);
  not not_6 (not_6_out, A18);
  not not_7 (not_7_out, A17);
  not not_8 (not_8_out, A16);
  nand nand_1 (nand_1_out, A15, 1'b1);
  nand nand_2 (nand_2_out, A14, A13, A12, A11, A10, A9, A8, A7);
  nand nand_3 (nand_3_out, not_4_out, not_3_out);
  nand nand_4 (nand_4_out, not_2_out, not_1_out);
  nand nand_5 (nand_5_out, not_1_out, not_2_out, not_3_out, not_4_out, not_5_out, not_6_out, not_7_out, not_8_out);
  nand nand_6 (nand_6_out, nand_1_out, nand_2_out);
  or or_1 (or_1_out, nand_3_out, nand_4_out);
  or or_2 (nRAM_EXT, not_5_out, or_1_out);
  or or_3 (nROM, nand_5_out, nand_1_out);
  nand nand_7 (nIO, nand_1_out, ~nand_5_out, ~nand_2_out);  // NAnd
  or or_4 (nRAM, nand_5_out, nand_6_out);

  // Notes on the sheet:
  //   11.5; 44.5
  //   10; 30
  //   HC30
  //   AHC00
  //   11; 38.5
  //   12.5; 53
  //   10; 53
  //   AHC32
  //   11.5; 67.5
  //   13.5; 61.5
  //   11; 61.5
  //   AHC138
  //   12.5; 70
  //   12; 76
  //   11; 79
  //   (11; 41.5 for select bits A4-A6)
  //   Worst case 79ns for I/O chip select
  //   Needs to happen 
  //   10ns before rising edge of clock for 65C22
  //   30ns before rising edge of clock for 65C51
  //   => half-period of clock >= 79+30 = 109ns
  //   => period of clock >= 218ns
  //   => frequency <= 4.58MHz
  //   for the ROM
  //   => half-period of clock >= 23.5+19+70 = 112.5ns
  //   => clock >= 225ns
  //         & clock >= 76+150+19 = 245ns
  //   => frequency <= 4.08Mhz
  //   AHC00: 1; 8.5
  //   AHC32: 1; 8.5
  //   HC30: 0; 23
  //   AHC138 act high: 1; 11.5
  //   AHC138 act low: 1; 11.5
  //   AHC138 select: 1; 11.5
endmodule

/* Test case:
A23 A22 A21 A20 A19 A18 A17 A16 A15 A14 A13 A12 A11 A10 A9 A8 A7   ~ROM ~RAM ~RAM_EXT ~IO
1   X   X   X   X   X   X   X   X   X   X   X   X   X   X  X  X    1    1     1     1
0   1   X   X   X   X   X   X   X   X   X   X   X   X   X  X  X    1    1     1     1
0   0   1   X   X   X   X   X   X   X   X   X   X   X   X  X  X    1    1     1     1
0   0   0   1   X   X   X   X   X   X   X   X   X   X   X  X  X    1    1     1     1
0   0   0   0   1   X   X   X   X   X   X   X   X   X   X  X  X    1    1     0     1
0   0   0   0   0   1   X   X   X   X   X   X   X   X   X  X  X    1    1     1     1
0   0   0   0   0   0   1   X   X   X   X   X   X   X   X  X  X    1    1     1     1
0   0   0   0   0   0   0   1   X   X   X   X   X   X   X  X  X    1    1     1     1
0   0   0   0   0   0   0   0   1   X   X   X   X   X   X  X  X    0    1     1     1
0   0   0   0   0   0   0   0   0   1   1   1   1   1   1  1  1    1    1     1     0
0   0   0   0   0   0   0   0   0   1   1   1   1   1   1  1  0    1    0     1     1
0   0   0   0   0   0   0   0   0   1   1   1   1   1   1  0  X    1    0     1     1
0   0   0   0   0   0   0   0   0   1   1   1   1   1   0  X  X    1    0     1     1
0   0   0   0   0   0   0   0   0   1   1   1   1   0   X  X  X    1    0     1     1
0   0   0   0   0   0   0   0   0   1   1   1   0   X   X  X  X    1    0     1     1
0   0   0   0   0   0   0   0   0   1   1   0   X   X   X  X  X    1    0     1     1
0   0   0   0   0   0   0   0   0   1   0   X   X   X   X  X  X    1    0     1     1
0   0   0   0   0   0   0   0   0   0   X   X   X   X   X  X  X    1    0     1     1
*/
