// Digital circuit clock_2.dig as structural Verilog
module clock_2 (
);

  wire and_1_out, and_2_out, and_3_out, and_4_out, and_5_out, and_6_out, and_7_out, and_8_out, CLK,
       d_ff_as_1_nq, d_ff_as_1_q, d_ff_as_2_nq, d_ff_as_2_q, d_ff_as_4_nq, FAST, FAST_out, FAST_SEL, HALT,
       nand_2_out, nand_3_out, nand_4_out, nBRK, nCLK, nFAST, nFAST_RST, nFAST_SET, nPULSE_RST, nPULSE_SEL,
       nSLOW, nSLOW_RST, nSTOP, or_2_out, or_3_out, or_4_out, PULSE, PULSE_out, PULSE_SEL, reset_1_out, SLOW,
       SLOW_out, SLOW_SEL;

  Button #(.activeLow("true")) BRK (.out(nBRK));
  Button u_HALT (.out(HALT));
  Button #(.activeLow("true")) u_FAST (.out(FAST_out));
  Button #(.activeLow("true")) u_SLOW (.out(SLOW_out));
  Button #(.activeLow("true")) u_PULSE (.out(PULSE_out));
  not not_1 (nFAST, FAST);
  Button button_1 (.out(FAST));
  Button button_2 (.out(SLOW));
  not not_2 (nSLOW, SLOW);
  nand nand_1 (PULSE, PULSE_out, 1'b1);
  Reset reset_1 (.out(reset_1_out));
  or or_1 (nFAST_RST, reset_1_out, 1'b0);
  nand nand_2 (nand_2_out, and_3_out, and_2_out);
  nand nand_3 (nand_3_out, and_1_out, and_3_out);
  nand nand_4 (nand_4_out, and_1_out, and_2_out);
  PullUp pullup_1 (.out(nFAST_RST));
  PullUp pullup_2 (.out(nSLOW_RST));
  PullUp pullup_3 (.out(nPULSE_RST));
  and and_1 (and_1_out, nand_2_out, nFAST_RST, FAST_out);
  and and_2 (and_2_out, nand_3_out, nSLOW_RST, SLOW_out);
  and and_3 (and_3_out, nand_4_out, nPULSE_RST, PULSE_out);
  or or_2 (or_2_out, nPULSE_SEL, and_1_out);
  or or_3 (or_3_out, nPULSE_SEL, and_2_out);
  PullUp pullup_4 (.out(nFAST_SET));
  PullUp pullup_5 (.out(nFAST_RST));
  PullUp pullup_6 (.out(nFAST_RST));
  and and_4 (and_4_out, nFAST_RST, or_2_out);
  and and_5 (and_5_out, nSLOW_RST, or_3_out);
  and and_6 (and_6_out, nSTOP, nFAST_RST);
  D_FF_AS d_ff_as_1 (.Set(~nFAST_SET), .D(and_1_out), .C(nCLK), .Clr(~and_4_out), .Q(d_ff_as_1_q), .nQ(d_ff_as_1_nq));
  D_FF_AS d_ff_as_2 (.Set(~nFAST_RST), .D(and_2_out), .C(nCLK), .Clr(~and_5_out), .Q(d_ff_as_2_q), .nQ(d_ff_as_2_nq));
  D_FF_AS d_ff_as_3 (.Set(~and_6_out), .D(and_3_out), .C(nCLK), .Clr(~nPULSE_RST), .Q(nPULSE_SEL), .nQ(PULSE_SEL));
  D_FF_AS d_ff_as_4 (.Set(~nFAST_RST), .D(1'b0), .C(HALT), .Clr(~1'b1), .Q(nSTOP), .nQ(d_ff_as_4_nq));
  LED led_1 (.in(d_ff_as_4_nq));
  and and_7 (and_7_out, nFAST_SET, nSTOP, d_ff_as_1_nq);
  and and_8 (and_8_out, nFAST_RST, nSTOP, d_ff_as_2_nq);
  Multiplexer #(.Selector_Bits(3)) multiplexer_1 (
    .sel({SLOW_SEL, FAST_SEL, PULSE_SEL}), .in_0(1'b0), .in_1(PULSE), .in_2(FAST), .in_3(FAST), .in_4(SLOW),
    .in_5(SLOW), .in_6(1'b0), .in_7(1'b0), .out(CLK));
  D_FF_AS d_ff_as_5 (.Set(~and_7_out), .D(d_ff_as_1_q), .C(nFAST), .Clr(~nFAST_RST), .nQ(FAST_SEL));  // open: Q
  D_FF_AS d_ff_as_6 (.Set(~and_8_out), .D(d_ff_as_2_q), .C(nSLOW), .Clr(~nSLOW_RST), .nQ(SLOW_SEL));  // open: Q
  or or_4 (or_4_out, CLK, 1'b0);
  not not_3 (nCLK, CLK);
  LED led_2 (.in(or_4_out));
  LED led_3 (.in(FAST_SEL));
  LED led_4 (.in(SLOW_SEL));
  LED led_5 (.in(PULSE_SEL));

  // Other names for the same wires on the sheet: nPULSE_SET = nFAST_RST; nPWRUP = nFAST_RST; nSLOW_SET = nFAST_RST
endmodule
