// Digital circuit glue.dig as structural Verilog
module glue (
  input  CLK_IN,
  input  BE,
  input  RDY,
  input  RnW,
  input  VA,
  input  RDY_REG,
  output L_OE,
  output B_OE,
  output L_LE,
  output nRD,
  output nWR,
  output nWAI
);

  wire CLK, CLK_plus, CLK_plus__OR_RDY_IN, CLK_t, nand_1_out, nand_4_out, nand_5_out, nand_6_out, nCLK,
       or_4_out;

  Delay #(.delayTime(10)) delay_1 (.in(CLK_IN), .out(CLK_t));
  Delay #(.delayTime(10)) delay_2 (.in(CLK_t), .out(CLK));
  // NOr nor_1 has open pins: In_1=1'b1, In_2=1'b1, out=open
  // NOr nor_2 has open pins: In_1=1'b1, In_2=1'b1, out=open
  nor nor_3 (nCLK, CLK, CLK);
  Delay #(.delayTime(10)) delay_3 (.in(CLK), .out(CLK_plus));
  // Or or_1 has open pins: In_1=1'b1, In_2=1'b1, out=open
  or or_2 (nWAI, RDY, RDY_REG);
  nand nand_1 (nand_1_out, 1'b1, 1'b1);
  not not_1 (RDY_REG, RDY_REG);
  // NAnd nand_2 has open pins: In_1=nand_1_out, In_2=nand_1_out, out=open
  nand nand_3 (L_OE, BE, BE);
  nand nand_4 (nand_4_out, RnW, RnW, RnW);
  or or_3 (CLK_plus__OR_RDY_IN, RDY_REG, CLK_plus);
  or or_4 (or_4_out, CLK_IN, RDY_REG);
  nor nor_4 (L_LE, CLK_plus__OR_RDY_IN, CLK);
  nand nand_5 (nand_5_out, CLK_plus__OR_RDY_IN, RnW, VA);
  nand nand_6 (nand_6_out, nand_4_out, VA, or_4_out);
  nand nand_7 (B_OE, CLK_plus__OR_RDY_IN, BE);
  assign nRD = ~L_OE ? nand_5_out : 1'bz;  // DriverInvSel driverinvsel_1
  assign nWR = ~L_OE ? nand_6_out : 1'bz;  // DriverInvSel driverinvsel_2

  // Other names for the same wires on the sheet: nRDY_REG = RDY_REG

  // Notes on the sheet:
  //   VDA/VPA -> VA
  //   VDA/VPA -> SYNC
endmodule

/* Test case:
RDY RDY_IN ~WAI
0   0      1
0   1      0
1   0      1
1   1      1
*/

/* Test case:
CLK_IN BE  RDY_IN L_LE B_OE L_OE 
0      0   0      0    1    1
1      0   0      0    1    1
0      1   0      0    0    0
1      1   0      0    0    0
0      0   1      1    1    1
1      0   1      0    1    1
0      1   1      1    1    0
1      1   1      0    0    0
*/

/* Test case:
CLK_IN R~W  VA  BE  RDY_IN ~RD  ~WR
0      0    0   0   0      Z    Z
1      0    0   0   0      Z    Z
0      1    0   0   0      Z    Z
1      1    0   0   0      Z    Z
0      0    1   0   0      Z    Z
1      0    1   0   0      Z    Z
0      1    1   0   0      Z    Z
1      1    1   0   0      Z    Z
0      0    0   0   1      Z    Z
1      0    0   0   1      Z    Z
0      1    0   0   1      Z    Z
1      1    0   0   1      Z    Z
0      0    1   0   1      Z    Z
1      0    1   0   1      Z    Z
0      1    1   0   1      Z    Z
1      1    1   0   1      Z    Z
0      0    0   1   0      1    1
1      0    0   1   0      1    1
0      1    0   1   0      1    1
1      1    0   1   0      1    1
0      0    1   1   0      1    0
1      0    1   1   0      1    0
0      1    1   1   0      0    1
1      1    1   1   0      0    1
0      0    0   1   1      1    1
1      0    0   1   1      1    1
0      1    0   1   1      1    1
1      1    0   1   1      1    1
0      0    1   1   1      1    1
1      0    1   1   1      1    0
0      1    1   1   1      1    1
1      1    1   1   1      0    1
*/
