// Digital circuit pulse.dig as structural Verilog
module pulse (
  input  RnW,
  input  CLK,
  input  VA,
  input  BE,
  input  RDY,
  output nRD,
  output nWR
);

  wire nand_1_out, nand_2_out, nand_3_out, not_1_out, not_2_out, not_3_out;

  not not_1 (not_1_out, BE);
  not not_2 (not_2_out, CLK);
  nand nand_1 (nand_1_out, not_2_out, RDY);
  not not_3 (not_3_out, RnW);
  nand nand_2 (nand_2_out, RnW, VA, nand_1_out);
  nand nand_3 (nand_3_out, not_3_out, VA, nand_1_out);
  assign nRD = ~not_1_out ? nand_2_out : 1'bz;  // DriverInvSel driverinvsel_1
  assign nWR = ~not_1_out ? nand_3_out : 1'bz;  // DriverInvSel driverinvsel_2
endmodule

/* Test case:
CLK R~W  VA  BE  RDY    ~RD  ~WR
0   0    0   0   0      Z    Z
1   0    0   0   0      Z    Z
0   1    0   0   0      Z    Z
1   1    0   0   0      Z    Z
0   0    1   0   0      Z    Z
1   0    1   0   0      Z    Z
0   1    1   0   0      Z    Z
1   1    1   0   0      Z    Z
0   0    0   0   1      Z    Z
1   0    0   0   1      Z    Z
0   1    0   0   1      Z    Z
1   1    0   0   1      Z    Z
0   0    1   0   1      Z    Z
1   0    1   0   1      Z    Z
0   1    1   0   1      Z    Z
1   1    1   0   1      Z    Z
0   0    0   1   0      1    1
1   0    0   1   0      1    1
0   1    0   1   0      1    1
1   1    0   1   0      1    1
0   0    1   1   0      1    0
1   0    1   1   0      1    0
0   1    1   1   0      0    1
1   1    1   1   0      0    1
0   0    0   1   1      1    1
1   0    0   1   1      1    1
0   1    0   1   1      1    1
1   1    0   1   1      1    1
0   0    1   1   1      1    1
1   0    1   1   1      1    0
0   1    1   1   1      1    1
1   1    1   1   1      0    1
*/
